# Fritzing sketch AntilogMM_Test (saved by Fritzing 0.9.4)
perfboards: 1

parts:
  J1 = female pin header, 3 pins [form="♀ (female)"]  # not connected
  J2 = female pin header, 2 pins [form="♀ (female)"]
  J3 = female pin header, 3 pins [form="♀ (female)"]  # not connected
  J4 = female pin header, 3 pins [form="♀ (female)"]
  R1 = Resistor [tolerance=±5% resistance=10k package=THT]
  J5 = female pin header, 2 pins [form="♀ (female)"]  # not connected

nets:
  N1: J2.pin2, R1.Pin_1
  N2: J4.pin3, R1.Pin_0

notes:
  Cutoff
  Out
  1 GND
  2 Out
  PWR_OUT
  VCC
  RL=10k ohm
  PSU
  Function Generator
  Triangle Wave
  GND
  Oscillo Scope
